// Logisim project cpu.circ as structural Verilog
module SingleReg (
  input  clk,
  input  reset,
  input  WrtEn,
  input  [15:0] datain,
  output [15:0] dataout
);

  wire clkin;

  and and_1 (clkin, clk, WrtEn);
  D_Flip_Flop d_ff_1 (.D(datain[15]), .clk(clkin), .Q(dataout[15]), .reset(reset));  // open: Qn, preset
  D_Flip_Flop d_ff_2 (.D(datain[13]), .clk(clkin), .Q(dataout[13]), .reset(reset));  // open: Qn, preset
  D_Flip_Flop d_ff_3 (.D(datain[11]), .clk(clkin), .Q(dataout[11]), .reset(reset));  // open: Qn, preset
  D_Flip_Flop d_ff_4 (.D(datain[9]), .clk(clkin), .Q(dataout[9]), .reset(reset));  // open: Qn, preset
  D_Flip_Flop d_ff_5 (.D(datain[7]), .clk(clkin), .Q(dataout[7]), .reset(reset));  // open: Qn, preset
  D_Flip_Flop d_ff_6 (.D(datain[5]), .clk(clkin), .Q(dataout[5]), .reset(reset));  // open: Qn, preset
  D_Flip_Flop d_ff_7 (.D(datain[3]), .clk(clkin), .Q(dataout[3]), .reset(reset));  // open: Qn, preset
  D_Flip_Flop d_ff_8 (.D(datain[1]), .clk(clkin), .Q(dataout[1]), .reset(reset));  // open: Qn, preset
  D_Flip_Flop d_ff_9 (.D(datain[14]), .clk(clkin), .Q(dataout[14]), .reset(reset));  // open: Qn, preset
  D_Flip_Flop d_ff_10 (.D(datain[12]), .clk(clkin), .Q(dataout[12]), .reset(reset));  // open: Qn, preset
  D_Flip_Flop d_ff_11 (.D(datain[10]), .clk(clkin), .Q(dataout[10]), .reset(reset));  // open: Qn, preset
  D_Flip_Flop d_ff_12 (.D(datain[8]), .clk(clkin), .Q(dataout[8]), .reset(reset));  // open: Qn, preset
  D_Flip_Flop d_ff_13 (.D(datain[6]), .clk(clkin), .Q(dataout[6]), .reset(reset));  // open: Qn, preset
  D_Flip_Flop d_ff_14 (.D(datain[4]), .clk(clkin), .Q(dataout[4]), .reset(reset));  // open: Qn, preset
  D_Flip_Flop d_ff_15 (.D(datain[2]), .clk(clkin), .Q(dataout[2]), .reset(reset));  // open: Qn, preset
  D_Flip_Flop d_ff_16 (.D(datain[0]), .clk(clkin), .Q(dataout[0]), .reset(reset));  // open: Qn, preset

  // Other names for the same wires on the sheet: b0 = datain[0]; b1 = datain[1]; b2 = datain[2]; b3 = datain[3];
  //   b4 = datain[4]; b5 = datain[5]; b6 = datain[6]; b7 = datain[7]; b8 = datain[8]; b9 = datain[9];
  //   b10 = datain[10]; b11 = datain[11]; b12 = datain[12]; b13 = datain[13]; b14 = datain[14]; b15 = datain[15];
  //   o0 = dataout[0]; o1 = dataout[1]; o2 = dataout[2]; o3 = dataout[3]; o4 = dataout[4]; o5 = dataout[5];
  //   o6 = dataout[6]; o7 = dataout[7]; o8 = dataout[8]; o9 = dataout[9]; o10 = dataout[10]; o11 = dataout[11];
  //   o12 = dataout[12]; o13 = dataout[13]; o14 = dataout[14]; o15 = dataout[15]
endmodule

module RegFile (
  input  reset,
  input  clk,
  input  WriteEnable,
  input  [2:0] read01,
  input  [15:0] datain,
  input  [2:0] writereg,
  input  [2:0] read02,
  output [15:0] dataout1,
  output [15:0] dataout2
);

  wire clk_t, decoder_1_out1, decoder_1_out2, decoder_1_out3, decoder_1_out4, decoder_1_out5, decoder_1_out6,
       decoder_1_out7, r10, r11, r12, r13, r14, r15, r16, r17, r20, r21, r22, r23, r24, r25, r26, r27,
       undriven, undriven_2;
  wire [15:0] r0_dataout, r1_dataout, r2_dataout, r3_dataout, r4_dataout, r5_dataout, r6_dataout, r7_dataout;

  and and_1 (clk_t, clk, WriteEnable);
  Decoder #(.select(3), .enable("false")) decoder_1 (
    .out1(decoder_1_out1), .out2(decoder_1_out2), .out3(decoder_1_out3), .out4(decoder_1_out4),
    .out5(decoder_1_out5), .out6(decoder_1_out6), .out7(decoder_1_out7), .sel(writereg));  // open: out0
  SingleReg r7 (.clk(clk_t), .reset(reset), .WrtEn(decoder_1_out7), .datain(datain), .dataout(r7_dataout));
  SingleReg r6 (.clk(clk_t), .reset(reset), .WrtEn(decoder_1_out6), .datain(datain), .dataout(r6_dataout));
  SingleReg r5 (.clk(clk_t), .reset(reset), .WrtEn(decoder_1_out5), .datain(datain), .dataout(r5_dataout));
  SingleReg r4 (.clk(clk_t), .reset(reset), .WrtEn(decoder_1_out4), .datain(datain), .dataout(r4_dataout));
  SingleReg r3 (.clk(clk_t), .reset(reset), .WrtEn(decoder_1_out3), .datain(datain), .dataout(r3_dataout));
  SingleReg r2 (.clk(clk_t), .reset(reset), .WrtEn(undriven), .datain(datain), .dataout(r2_dataout));
  SingleReg r1 (.clk(clk_t), .reset(reset), .WrtEn(undriven_2), .datain(datain), .dataout(r1_dataout));
  SingleReg r0 (.clk(clk_t), .reset(reset), .WrtEn(1'b0), .datain({16{1'b0}}), .dataout(r0_dataout));
  assign dataout1 = r17 ? r7_dataout : 16'bz;  // Controlled_Buffer controlled_buffer_1
  assign dataout1 = r16 ? r6_dataout : 16'bz;  // Controlled_Buffer controlled_buffer_2
  assign dataout1 = r15 ? r5_dataout : 16'bz;  // Controlled_Buffer controlled_buffer_3
  assign dataout1 = r14 ? r4_dataout : 16'bz;  // Controlled_Buffer controlled_buffer_4
  assign dataout1 = r13 ? r3_dataout : 16'bz;  // Controlled_Buffer controlled_buffer_5
  assign dataout1 = r12 ? r2_dataout : 16'bz;  // Controlled_Buffer controlled_buffer_6
  assign dataout1 = r11 ? r1_dataout : 16'bz;  // Controlled_Buffer controlled_buffer_7
  assign dataout1 = r10 ? r0_dataout : 16'bz;  // Controlled_Buffer controlled_buffer_8
  assign dataout2 = r27 ? r7_dataout : 16'bz;  // Controlled_Buffer controlled_buffer_9
  assign dataout2 = r26 ? r6_dataout : 16'bz;  // Controlled_Buffer controlled_buffer_10
  assign dataout2 = r25 ? r5_dataout : 16'bz;  // Controlled_Buffer controlled_buffer_11
  assign dataout2 = r24 ? r4_dataout : 16'bz;  // Controlled_Buffer controlled_buffer_12
  assign dataout2 = r23 ? r3_dataout : 16'bz;  // Controlled_Buffer controlled_buffer_13
  assign dataout2 = r22 ? r2_dataout : 16'bz;  // Controlled_Buffer controlled_buffer_14
  assign dataout2 = r21 ? r1_dataout : 16'bz;  // Controlled_Buffer controlled_buffer_15
  assign dataout2 = r20 ? r0_dataout : 16'bz;  // Controlled_Buffer controlled_buffer_16
  Decoder #(.select(3), .enable("false")) decoder_2 (
    .out0(r10), .out1(r11), .out2(r12), .out3(r13), .out4(r14), .out5(r15), .out6(r16), .out7(r17),
    .sel(read01));
  Decoder #(.select(3), .enable("false")) decoder_3 (
    .out0(r20), .out1(r21), .out2(r22), .out3(r23), .out4(r24), .out5(r25), .out6(r26), .out7(r27),
    .sel(read02));

  // Other names for the same wires on the sheet: R = reset
endmodule
